// Logisim project VHDL1.circ as structural Verilog
module main (
  input  [2:0] in_1,
  input  in_2,
  input  in_3,
  input  in_4,
  input  in_5,
  input  in_6,
  input  in_7,
  input  in_8,
  input  in_9,
  input  in_10,
  input  in_11,
  input  in_12,
  input  in_13,
  input  in_14,
  input  in_15,
  input  in_16,
  input  in_17,
  input  in_18,
  input  in_19,
  input  in_20,
  input  [2:0] in_21,
  input  in_22,
  input  in_23,
  input  in_24,
  input  in_25,
  input  in_26,
  input  in_27,
  input  in_28,
  input  in_29,
  input  in_30,
  input  in_31,
  input  in_32,
  input  in_33,
  input  in_34,
  input  in_35,
  input  in_36,
  input  in_37,
  input  in_38,
  input  in_39,
  input  in_40,
  input  in_41,
  input  in_42,
  input  in_43,
  input  in_44,
  input  in_45,
  input  in_46,
  input  in_47,
  input  in_48,
  input  in_49,
  input  in_50,
  input  in_51,
  input  in_52,
  input  in_53,
  output out_54,
  output out_55,
  output out_56,
  output out_57
);

  wire [7:0] counter7seg_1_display, segment_letters_1_display;

  logic_test logic_test_1 (.a(in_2), .b(in_3), .c(in_4), .d(in_5), .out1(out_54), .out2(out_55));
  mux8_1 mux8_1_1 (
    .a(in_6), .b(in_7), .c(in_9), .d(in_11), .e(in_13), .f(in_15), .g(in_17), .h(in_19), .ch(in_21),
    .data(out_56));
  counter7seg counter7seg_1 (
    .vt({in_53, in_52, in_51, in_50, in_48, in_46, in_44, in_41, in_39, in_37, in_35, in_33, in_31}),
    .en(in_42), .display(counter7seg_1_display));
  _7_Segment_Display u_7_segment_display_1 (
    .g(counter7seg_1_display[1]), .f(counter7seg_1_display[2]), .a(counter7seg_1_display[7]),
    .b(counter7seg_1_display[6]), .e(counter7seg_1_display[3]), .d(counter7seg_1_display[4]),
    .c(counter7seg_1_display[5]), .dp(counter7seg_1_display[0]));
  segment_letters segment_letters_1 (.ch(in_1), .display(segment_letters_1_display));
  _7_Segment_Display u_7_segment_display_2 (
    .g(segment_letters_1_display[1]), .f(segment_letters_1_display[2]), .a(segment_letters_1_display[7]),
    .b(segment_letters_1_display[6]), .e(segment_letters_1_display[3]), .d(segment_letters_1_display[4]),
    .c(segment_letters_1_display[5]), .dp(segment_letters_1_display[0]));
  vote25 vote25_1 (
    .vt({in_49, in_47, in_45, in_43, in_40, in_38, in_36, in_34, in_32, in_30, in_29, in_28, in_27, in_26, in_25, in_24, in_23, in_22, in_20, in_18, in_16, in_14, in_12, in_10, in_8}),
    .result(out_57));
endmodule

// VHDL entity logic_test, as the project stores it:
library ieee;
use ieee.std_logic_1164.all;

entity logic_test is
    port(
        a, b, c, d : in std_logic;
        out1, out2 : out std_logic
    );
end entity logic_test;

architecture bhv of logic_test is
begin
    out1 <= a and b and c and d;
    out2 <= a or b or c or d;
end architecture bhv;

// VHDL entity mux8_1, as the project stores it:
library ieee;
use ieee.std_logic_1164.all;

entity mux8_1 is
    port(
        a, b, c, d, e, f, g, h : in std_logic;
        ch : in std_logic_vector(2 downto 0);
        data : out std_logic
    );
end entity mux8_1;

architecture bhv of mux8_1 is
begin
    process(a, b, c, d, e, f, g, h, ch)
    begin
        case ch is
            when "000" => data <= a;
            when "001" => data <= b;
            when "010" => data <= c;
            when "011" => data <= d;
            when "100" => data <= e;
            when "101" => data <= f;
            when "110" => data <= g;
            when "111" => data <= h;
            when others => data <= '0';
        end case;
    end process;
end architecture bhv;

// VHDL entity segment_letters, as the project stores it:
library ieee;
use ieee.std_logic_1164.all;

entity segment_letters is
    port(
        ch : in std_logic_vector(2 downto 0);
        display : out std_logic_vector(7 downto 0)
    );
end entity segment_letters;

architecture bhv of segment_letters is
begin
    process(ch)
    begin
        case ch is
            -- Bit order: a b c d e f g dp
            when "000" => display <= "11111010"; -- a
            when "001" => display <= "00111110"; -- b
            when "010" => display <= "00011010"; -- c
            when "011" => display <= "01111010"; -- d
            when "100" => display <= "10001110"; -- f
            when "101" => display <= "11110110"; -- g
            when others => display <= "00000000";
        end case;
    end process;
end architecture bhv;

// VHDL entity vote25, as the project stores it:
library ieee;
use ieee.std_logic_1164.all;

entity vote25 is
    port(
        vt : in std_logic_vector(24 downto 0);
        result : out std_logic
    );
end entity vote25;

architecture bhv of vote25 is
begin
    process(vt)
        variable sum : integer range 0 to 25;
    begin
        sum := 0;

        for i in 0 to 24 loop
            if vt(i) = '1' then
                sum := sum + 1;
            end if;
        end loop;

        if sum >= 13 then
            result <= '1';
        else
            result <= '0';
        end if;
    end process;
end architecture bhv;

// VHDL entity counter7seg, as the project stores it:
library ieee;
use ieee.std_logic_1164.all;

entity counter7seg is
    port(
        vt      : in std_logic_vector(12 downto 0);
        en      : in std_logic;
        display : out std_logic_vector(7 downto 0)
    );
end entity counter7seg;

architecture bhv of counter7seg is
begin
    process(vt, en)
        variable sum : integer range 0 to 15;
    begin
        sum := 0;

        for i in 0 to 12 loop
            if vt(i) = '1' then
                sum := sum + 1;
            end if;
        end loop;

        if en = '0' then
            display <= "00000000";
        else
            case sum is
                -- Bit order: a b c d e f g dp
                when 0  => display <= "11111100";
                when 1  => display <= "01100000";
                when 2  => display <= "11011010";
                when 3  => display <= "11110010";
                when 4  => display <= "01100110";
                when 5  => display <= "10110110";
                when 6  => display <= "10111110";
                when 7  => display <= "11100000";
                when 8  => display <= "11111110";
                when 9  => display <= "11110110";
                when 10 => display <= "11101110"; -- A
                when 11 => display <= "00111110"; -- b
                when 12 => display <= "10011100"; -- C
                when 13 => display <= "01111010"; -- d
                when 14 => display <= "10011110"; -- E
                when 15 => display <= "10001110"; -- F
                when others => display <= "00000000";
            end case;
        end if;
    end process;
end architecture bhv;
